# Fritzing sketch mini (saved by Fritzing 0.9.4)

parts:
  F1 = Fan - 4 wire [package=THT]
  Bauteil3 = Arduino Pro Mini v13

nets:
  GND: F1.GND, Bauteil3.GND
  N1: F1.Power, Bauteil3.VCC
  N2: F1.PWM, Bauteil3.D2
  N3: F1.Tach, Bauteil3.D3_PWM

custom parts:
  Fan - 4 wire: Fan, 4 wire with tach.
