# Fritzing sketch simple (saved by Fritzing 0.9.4)

parts:
  F1 = Fan - 4 wire [package=THT]
  Bauteil1 = Arduino Uno (Rev3) - ICSP

nets:
  GND: F1.GND, Bauteil1.GND
  N1: F1.Power, Bauteil1.5V
  N2: F1.PWM, Bauteil1.D2
  N3: F1.Tach, Bauteil1.D3_PWM

custom parts:
  Fan - 4 wire: Fan, 4 wire with tach.
